// Logisim project Data Path.circ as structural Verilog: 2 circuits, main circuit Data Path
module Data_Path (
);

  wire next_pc_1_pcsrc, Rs__Rt;
  wire [2:0] multiplexer_2_out, spliter_1_rd, spliter_1_rs, spliter_1_rt;
  wire [5:0] Imm6;
  wire [11:0] adder_1_out, Imm12, multiplexer_1_out, next_pc_1_next_pc, PC_q;
  wire [15:0] alu_1_alu_output, bit_extender_1_out, multiplexer_3_out, multiplexer_4_out, ram_1_data,
       register_file_1_rs_data, register_file_1_rt_data, rom_1_data;

  Adder #(.width(12)) adder_1 (.a(PC_q), .b(12'h1), .out(adder_1_out));  // open: cin, cout
  Multiplexer #(.width(12), .enable("false")) multiplexer_1 (
    .in0(adder_1_out), .in1(next_pc_1_next_pc), .out(multiplexer_1_out), .sel(next_pc_1_pcsrc));
  Register #(.width(12)) PC (.D(multiplexer_1_out), .Q(PC_q));  // open: en, clk, clr
  Next_PC next_pc_1 (
    .PC(PC_q), .Imm6(Imm6), .Imm12(Imm12), .next_PC(next_pc_1_next_pc), .PCSrc(next_pc_1_pcsrc),
    .Rs__Rt(Rs__Rt));  // open: Bne, J, Beq
  Spliter spliter_1 (
    .in_1(rom_1_data), .Rt(spliter_1_rt), .Imm6(Imm6), .Rs(spliter_1_rs), .Rd(spliter_1_rd), .Imm12(Imm12));  // open: f, Op
  ROM #(.addrWidth(12), .dataWidth(16)) rom_1 (.addr(PC_q), .data(rom_1_data));  // open: sel
  Multiplexer #(.width(3), .enable("false")) multiplexer_2 (
    .in0(spliter_1_rt), .in1(spliter_1_rd), .out(multiplexer_2_out));  // open: sel
  Register_File register_file_1 (
    .Rd_adrress(multiplexer_2_out), .Rs_data(register_file_1_rs_data), .Rt_data(register_file_1_rt_data),
    .Rd_data(multiplexer_4_out), .Rs_address(spliter_1_rs), .Rt_address(spliter_1_rt));  // open: RegWrite
  assign bit_extender_1_out = {{10{Imm6[5]}}, Imm6};  // Bit_Extender bit_extender_1
  Multiplexer #(.width(16), .enable("false")) multiplexer_3 (
    .in0(register_file_1_rt_data), .in1(bit_extender_1_out), .out(multiplexer_3_out));  // open: sel
  ALU alu_1 (
    .Rs(register_file_1_rs_data), .Rt(multiplexer_3_out), .ALU_Output(alu_1_alu_output), .Rs_Rt(Rs__Rt));  // open: ALUCtrl
  RAM #(.addrWidth(16), .dataWidth(16), .bus("separate")) ram_1 (
    .addr(alu_1_alu_output), .din(register_file_1_rt_data), .data(ram_1_data));  // open: str, sel, clk, ld, clr
  Multiplexer #(.width(16), .enable("false")) multiplexer_4 (
    .in0(alu_1_alu_output), .in1(ram_1_data), .out(multiplexer_4_out));  // open: sel
endmodule

module Control (
  input  op3,
  input  op2,
  input  op1,
  input  op0,
  output RegDst,
  output RegWrite,
  output ExtOp,
  output ALUSrc,
  output MemWrite,
  output MemRead,
  output MemtoReg,
  output J,
  output Beq,
  output Bne,
  output ALUOp
);

  wire and_1_out, and_2_out, and_3_out, and_4_out, and_5_out, and_6_out, and_8_out, and_9_out, not_1_out,
       not_2_out, not_3_out, not_4_out, not_5_out, not_6_out, not_7_out, not_8_out, not_9_out, not_10_out,
       not_11_out, not_12_out, not_13_out, not_14_out, not_15_out, not_16_out, not_17_out, not_18_out,
       not_19_out;

  not not_1 (not_1_out, op3);
  and and_1 (and_1_out, not_1_out, not_2_out);
  not not_2 (not_2_out, op2);
  not not_3 (not_3_out, op2);
  and and_2 (and_2_out, not_3_out, op0);
  not not_4 (not_4_out, op3);
  and and_3 (and_3_out, not_4_out, not_5_out);
  not not_5 (not_5_out, op1);
  not not_6 (not_6_out, op3);
  and and_4 (and_4_out, not_6_out, not_7_out);
  not not_7 (not_7_out, op0);
  not not_8 (not_8_out, op2);
  and and_5 (and_5_out, not_8_out, not_9_out);
  not not_9 (not_9_out, op0);
  not not_10 (not_10_out, op2);
  or or_1 (ExtOp, not_10_out, op1);
  and and_6 (and_6_out, op3, not_11_out);
  not not_11 (not_11_out, op0);
  not not_12 (not_12_out, op3);
  not not_13 (not_13_out, op3);
  not not_14 (not_14_out, op0);
  not not_15 (not_15_out, op3);
  and and_7 (MemtoReg, not_15_out, op1);
  and and_8 (and_8_out, op3, op2, not_16_out);
  not not_16 (not_16_out, op1);
  and and_9 (and_9_out, op3, op2, op0);
  not not_17 (not_17_out, op2);
  not not_18 (not_18_out, op1);
  not not_19 (not_19_out, op2);
  or or_2 (RegDst, and_1_out, and_2_out);
  or or_3 (RegWrite, and_3_out, and_4_out, and_5_out);
  or or_4 (ALUSrc, op2, and_6_out);
  and and_10 (MemWrite, not_12_out, op2, op1, op0);
  and and_11 (MemRead, not_13_out, op2, op1, not_14_out);
  or or_5 (J, and_8_out, and_9_out);
  and and_12 (Beq, op3, not_17_out, not_18_out, op0);
  and and_13 (Bne, op3, not_19_out, op1, op0);
endmodule
