// Logisim project Next PC.circ as structural Verilog: 1 circuit, main circuit Next PC
module Next_PC (
  input  [11:0] PC,
  input  [5:0] Imm6,
  input  [11:0] Imm12,
  input  Bne,
  input  Rs__Rt,
  input  Beq,
  input  J,
  output PCSrc,
  output [11:0] next_PC
);

  wire and_1_out, and_2_out;
  wire [11:0] adder_1_out, bit_extender_1_out;

  assign bit_extender_1_out = {{6{Imm6[5]}}, Imm6};  // Bit_Extender bit_extender_1
  Adder #(.width(12)) adder_1 (.a(PC), .b(bit_extender_1_out), .out(adder_1_out));  // open: cin, cout
  Multiplexer #(.width(12), .enable("false")) multiplexer_1 (.in0(adder_1_out), .in1(Imm12), .out(next_PC), .sel(J));
  and and_1 (and_1_out, Bne, ~Rs__Rt);  // AND_Gate
  or or_1 (PCSrc, and_1_out, J, and_2_out);
  and and_2 (and_2_out, Rs__Rt, Beq);
endmodule
