// Logisim project Register File.circ as structural Verilog: 1 circuit, main circuit Register File
module Register_File (
  input  [2:0] Rd_adrress,
  input  [15:0] Rd_data,
  input  RegWrite,
  input  [2:0] Rs_address,
  input  [2:0] Rt_address,
  output [15:0] Rs_data,
  output [15:0] Rt_data
);

  wire and_1_out, and_2_out, and_3_out, and_4_out, and_5_out, and_6_out, and_7_out, decoder_1_out1,
       decoder_1_out2, decoder_1_out3, decoder_1_out4, decoder_1_out5, decoder_1_out6, decoder_1_out7,
       decoder_2_out0, decoder_2_out1, decoder_2_out2, decoder_2_out3, decoder_2_out4, decoder_2_out5,
       decoder_2_out6, decoder_2_out7, decoder_3_out0, decoder_3_out1, decoder_3_out2, decoder_3_out3,
       decoder_3_out4, decoder_3_out5, decoder_3_out6, decoder_3_out7;
  wire [15:0] register_1_q, register_2_q, register_3_q, register_4_q, register_5_q, register_6_q,
       register_7_q;

  Decoder #(.select(3), .enable("false")) decoder_1 (
    .out1(decoder_1_out1), .out2(decoder_1_out2), .out3(decoder_1_out3), .out4(decoder_1_out4),
    .out5(decoder_1_out5), .out6(decoder_1_out6), .out7(decoder_1_out7), .sel(Rd_adrress));  // open: out0
  Clock clock_1 (.out(decoder_1_out7));
  and and_1 (and_1_out, RegWrite, decoder_1_out1);
  and and_2 (and_2_out, RegWrite, decoder_1_out2);
  and and_3 (and_3_out, RegWrite, decoder_1_out3);
  and and_4 (and_4_out, RegWrite, decoder_1_out4);
  and and_5 (and_5_out, RegWrite, decoder_1_out5);
  and and_6 (and_6_out, RegWrite, decoder_1_out6);
  and and_7 (and_7_out, RegWrite, decoder_1_out7);
  Register #(.width(16)) register_1 (.D(Rd_data), .Q(register_1_q), .clk(and_1_out));  // open: en, clr
  Register #(.width(16)) register_2 (.D(Rd_data), .Q(register_2_q), .clk(and_2_out));  // open: en, clr
  Register #(.width(16)) register_3 (.D(Rd_data), .Q(register_3_q), .clk(and_3_out));  // open: en, clr
  Register #(.width(16)) register_4 (.D(Rd_data), .Q(register_4_q), .clk(and_4_out));  // open: en, clr
  Register #(.width(16)) register_5 (.D(Rd_data), .Q(register_5_q), .clk(and_5_out));  // open: en, clr
  Register #(.width(16)) register_6 (.D(Rd_data), .Q(register_6_q), .clk(and_6_out));  // open: en, clr
  Register #(.width(16)) register_7 (.D(Rd_data), .Q(register_7_q), .clk(and_7_out));  // open: en, clr
  Decoder #(.select(3), .enable("false")) decoder_2 (
    .out0(decoder_2_out0), .out1(decoder_2_out1), .out2(decoder_2_out2), .out3(decoder_2_out3),
    .out4(decoder_2_out4), .out5(decoder_2_out5), .out6(decoder_2_out6), .out7(decoder_2_out7),
    .sel(Rs_address));
  assign Rs_data = decoder_2_out1 ? register_1_q : 16'bz;  // Controlled_Buffer controlled_buffer_1
  assign Rs_data = decoder_2_out2 ? register_2_q : 16'bz;  // Controlled_Buffer controlled_buffer_2
  assign Rs_data = decoder_2_out3 ? register_3_q : 16'bz;  // Controlled_Buffer controlled_buffer_3
  assign Rs_data = decoder_2_out4 ? register_4_q : 16'bz;  // Controlled_Buffer controlled_buffer_4
  assign Rs_data = decoder_2_out5 ? register_5_q : 16'bz;  // Controlled_Buffer controlled_buffer_5
  assign Rs_data = decoder_2_out6 ? register_6_q : 16'bz;  // Controlled_Buffer controlled_buffer_6
  assign Rs_data = decoder_2_out7 ? register_7_q : 16'bz;  // Controlled_Buffer controlled_buffer_7
  assign Rt_data = decoder_3_out1 ? register_1_q : 16'bz;  // Controlled_Buffer controlled_buffer_8
  Decoder #(.select(3), .enable("false")) decoder_3 (
    .out0(decoder_3_out0), .out1(decoder_3_out1), .out2(decoder_3_out2), .out3(decoder_3_out3),
    .out4(decoder_3_out4), .out5(decoder_3_out5), .out6(decoder_3_out6), .out7(decoder_3_out7),
    .sel(Rt_address));
  assign Rt_data = decoder_3_out2 ? register_2_q : 16'bz;  // Controlled_Buffer controlled_buffer_9
  assign Rt_data = decoder_3_out3 ? register_3_q : 16'bz;  // Controlled_Buffer controlled_buffer_10
  assign Rt_data = decoder_3_out4 ? register_4_q : 16'bz;  // Controlled_Buffer controlled_buffer_11
  assign Rt_data = decoder_3_out5 ? register_5_q : 16'bz;  // Controlled_Buffer controlled_buffer_12
  assign Rt_data = decoder_3_out6 ? register_6_q : 16'bz;  // Controlled_Buffer controlled_buffer_13
  assign Rt_data = decoder_3_out7 ? register_7_q : 16'bz;  // Controlled_Buffer controlled_buffer_14
  // also tied to GND on the sheet: {decoder_2_out0, decoder_3_out0}
endmodule
